// Logisim project ALU16-Hack.circ as structural Verilog: 3 circuits, main circuit main
module main (
  input  in_1,
  input  in_2,
  input  in_3,
  input  in_4,
  input  in_5,
  input  in_6,
  input  [15:0] in_7,
  input  [15:0] in_8,
  output [15:0] out_9,
  output out_10,
  output out_11
);

  ALU alu_1 (
    .X(in_7), .Y(in_8), .ZX(in_1), .NX(in_2), .ZY(in_3), .NY(in_4), .F(in_5), .NO(in_6), .NG(out_11),
    .ZR(out_10), .Out(out_9));
endmodule

module ALU (
  input  ZX,
  input  NX,
  input  ZY,
  input  NY,
  input  F,
  input  NO,
  input  [15:0] X,
  input  [15:0] Y,
  output [15:0] Out,
  output NG,
  output ZR
);

  wire or_1_out;
  wire [15:0] adder_1_out, and_1_out, multiplexer_1_out, multiplexer_2_out, multiplexer_3_out,
       multiplexer_4_out, multiplexer_5_out, not_1_out, not_2_out, not_4_out;

  Multiplexer #(.width(16), .enable("false")) multiplexer_1 (
    .in0(X), .in1({16{1'b0}}), .out(multiplexer_1_out), .sel(ZX));
  Multiplexer #(.width(16), .enable("false")) multiplexer_2 (
    .in0(Y), .in1({16{1'b0}}), .out(multiplexer_2_out), .sel(ZY));
  assign not_1_out = ~multiplexer_1_out;  // NOT_Gate not_1, 16 bits wide
  assign not_2_out = ~multiplexer_2_out;  // NOT_Gate not_2, 16 bits wide
  Multiplexer #(.width(16), .enable("false")) multiplexer_3 (
    .in0(multiplexer_1_out), .in1(not_1_out), .out(multiplexer_3_out), .sel(NX));
  Multiplexer #(.width(16), .enable("false")) multiplexer_4 (
    .in0(multiplexer_2_out), .in1(not_2_out), .out(multiplexer_4_out), .sel(NY));
  assign and_1_out = multiplexer_3_out & multiplexer_4_out;  // AND_Gate and_1, 16 bits wide
  Adder #(.width(16)) adder_1 (.a(multiplexer_3_out), .b(multiplexer_4_out), .out(adder_1_out));  // open: cin, cout
  or or_1 (or_1_out, NG, Out[14], Out[13], Out[12], Out[11], Out[10], Out[9], Out[8], Out[7], Out[6], Out[5], Out[4], Out[3], Out[2], Out[1], Out[0]);
  not not_3 (ZR, or_1_out);
  Multiplexer #(.width(16), .enable("false")) multiplexer_5 (
    .in0(and_1_out), .in1(adder_1_out), .out(multiplexer_5_out), .sel(F));
  assign not_4_out = ~multiplexer_5_out;  // NOT_Gate not_4, 16 bits wide
  Multiplexer #(.width(16), .enable("false")) multiplexer_6 (
    .in0(multiplexer_5_out), .in1(not_4_out), .out({NG, Out[14:0]}), .sel(NO));

  assign Out[15] = NG;
endmodule

module CPU (
  input  [15:0] In,
  input  Clock,
  input  [15:0] InM,
  input  Reset,
  output [15:0] OutM
);

  wire not_1_out, undriven, undriven_2, undriven_3;
  wire [15:0] A_q, D_q, multiplexer_1_out, multiplexer_2_out, PC_q;

  Multiplexer #(.width(16), .enable("false")) multiplexer_1 (
    .in0(OutM), .in1(In), .out(multiplexer_1_out));  // open: sel
  Register #(.width(16)) A (.D(multiplexer_1_out), .en(undriven), .Q(A_q), .clk(Clock));  // open: clr
  Register #(.width(16)) D (.D(OutM), .en(undriven_2), .Q(D_q), .clk(Clock));  // open: clr
  Multiplexer #(.width(16), .enable("false")) multiplexer_2 (
    .in0(A_q), .in1(InM), .out(multiplexer_2_out));  // open: sel
  not not_1 (not_1_out, undriven_3);
  Counter #(.width(16), .max('hffff)) PC (
    .load(undriven_3), .D(A_q), .count(not_1_out), .Q(PC_q), .clk(Clock), .clr(Reset));  // open: carry
  ALU alu_1 (.X(D_q), .Y(multiplexer_2_out), .Out(OutM));  // open: ZX, NX, ZY, NY, F, NO, NG, ZR
endmodule
